# Fritzing sketch 3 - Stepper Motor (saved by Fritzing 0.9.3b)
breadboards: 1

parts:
  IC1 = ULN2003A [package="SO16 [SMD]"]
  LED1 = LED - 5mm [color="Red (633nm)" package="5 mm [THT]"]
  LED2 = LED - 5mm [color="Red (633nm)" package="5 mm [THT]"]
  LED3 = LED - 5mm [color="Red (633nm)" package="5 mm [THT]"]
  LED4 = LED - 5mm [color="Red (633nm)" package="5 mm [THT]"]
  R1 = Resistor [tolerance=±5% resistance=220 package=THT]
  M2 = Stepper Motor - Unipolar
  Raspberry_Pi_1 = Raspberry Pi 3 [part_number=RPI-3-V1.2]

nets:
  N1: IC1.In_1, LED1.anode, Raspberry_Pi_1.GPIO21
  N2: IC1.In_2, LED2.anode, Raspberry_Pi_1.GPIO26
  N3: IC1.In_3, LED3.anode, Raspberry_Pi_1.GPIO19
  N4: IC1.In_4, LED4.anode, Raspberry_Pi_1.GPIO13
  N5: IC1.0V, R1.Pin_1, Raspberry_Pi_1.GND
  N6: IC1.COM_-_Common, M2.COMMON_1, M2.COMMON_2, Raspberry_Pi_1.5V
  N7: IC1.Out_4, M2.D
  N8: IC1.Out_3, M2.B
  N9: IC1.Out_2, M2.C
  N10: IC1.Out_1, M2.A
  N11: LED1.cathode, LED2.cathode, LED3.cathode, LED4.cathode, R1.Pin_0
