# Fritzing sketch 4 - GPIO Input (saved by Fritzing 0.9.3b)
circuit board: 8.46667cm x 5.64444cm
breadboards: 1

parts:
  Raspberry_Pi_1 = Raspberry Pi 3 [part_number=RPI-3-V1.2]
  R1 = Resistor [tolerance=±5% resistance=330 package=THT]
  S1 = Pushbutton [package="[THT]"]
  LED1 = LED - 5mm [color="Red (633nm)" package="5 mm [THT]"]
  R2 = Resistor [tolerance=±5% resistance=330 package=THT]

nets:
  N1: Raspberry_Pi_1.3v3, R1.Pin_1
  N2: Raspberry_Pi_1.GND, R2.Pin_0
  N3: Raspberry_Pi_1.GPIO17, S1.Pin_1, S1.Pin_2
  N4: Raspberry_Pi_1.GPIO21, LED1.cathode
  N5: R1.Pin_0, S1.Pin_3, S1.Pin_4
  N6: LED1.anode, R2.Pin_1
